# Fritzing sketch vezje1 (saved by Fritzing 0.9.3b)
breadboards: 1

parts:
  SparkFun_ESP32_Thing1 = SparkFun ESP32 Thing [part_number=DEV-13907]
  U2 = POT [package=pot_mammoth]
  M1 = Humidity and Temperature Sensor DHT11
  SG1 = Buzzer 12mm [package=buzzer-12mm-ns]
  Water_Level_Sensor1 = Water Level Sensor
  R1 = Resistor [tolerance=±5% resistance=220 package="2512 [SMD]"]
  R2 = Resistor [tolerance=±5% resistance=220 package="2512 [SMD]"]
  R3 = Resistor [tolerance=±5% resistance=220 package="2512 [SMD]"]
  LED1 = LED - 3mm [color="Red (633nm)" package="3 mm [THT]"]
  LED2 = LED - 3mm [color="Yellow (595nm)" package="3 mm [THT]"]
  LED3 = LED - 3mm [color="Green (570nm)" package="3 mm [THT]"]

nets:
  N1: SparkFun_ESP32_Thing1.V_BATT, M1.Data, Water_Level_Sensor1.VCC
  N2: SparkFun_ESP32_Thing1.25, Water_Level_Sensor1.SIG
  N3: SparkFun_ESP32_Thing1.32K_XN, U2.A
  GND: SparkFun_ESP32_Thing1.GND, U2.E, M1.GND, SG1.1, Water_Level_Sensor1.GND, LED1.cathode, LED2.cathode, LED3.cathode
  N4: SparkFun_ESP32_Thing1.3.3V, U2.S
  N5: SparkFun_ESP32_Thing1.17, M1.Vcc
  N6: SparkFun_ESP32_Thing1.5, R1.Pin_0
  N7: SparkFun_ESP32_Thing1.18, R2.Pin_0
  N8: SparkFun_ESP32_Thing1.23, SG1.2
  N9: SparkFun_ESP32_Thing1.19, R3.Pin_0
  N10: R1.Pin_1, LED1.anode
  N11: R2.Pin_1, LED2.anode
  N12: R3.Pin_1, LED3.anode

custom parts:
  SparkFun ESP32 Thing: The SparkFun ESP32 Thing is a comprehensive development platform for Espressif’s ESP32, their super-charged version of the popular ESP8266. Like the 8266, the ESP32 is a WiFi-compatible microcontroller, but to that it adds support for Bluetooth low-energy (i.e BLE, BT4.0, Bluetooth Smart), and nearly 30 I/O pins. The ESP32’s power and versatility will make it the foundation of IoT and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
  Humidity and Temperature Sensor DHT11: Digital relative humidity & temperature sensor DHT11
  Water Level Sensor: A water level sensor. This sensor operates at 3V to 5V. The Sig (signal) pin outputs an analogue signal that is in proportion to the amount of water in contact with the sensor.
